// Logisim project 7Seg_Hex_Display.circ as structural Verilog: 8 circuits, main circuit main
module main (
  input  c0,
  input  c1,
  input  c2,
  input  c3
);

  wire sega_1_seg_a, segb_1_seg_b, segc_1_seg_c, segd_1_seg_d, sege_1_seg_e, segf_1_seg_f, segg_1_seg_g;

  SegA sega_1 (.x0(c0), .x1(c1), .x2(c2), .x3(c3), .SEG_A(sega_1_seg_a));
  SegB segb_1 (.x0(c0), .x1(c1), .x2(c2), .x3(c3), .SEG_B(segb_1_seg_b));
  SegC segc_1 (.x0(c0), .x1(c1), .x2(c2), .x3(c3), .SEG_C(segc_1_seg_c));
  SegD segd_1 (.x0(c0), .x1(c1), .x2(c2), .x3(c3), .SEG_D(segd_1_seg_d));
  SegE sege_1 (.x0(c0), .x1(c1), .x2(c2), .x3(c3), .SEG_E(sege_1_seg_e));
  SegF segf_1 (.x0(c0), .x1(c1), .x2(c2), .x3(c3), .SEG_F(segf_1_seg_f));
  SegG segg_1 (.x0(c0), .x1(c1), .x2(c2), .x3(c3), .SEG_G(segg_1_seg_g));
  _7_Segment_Display u_7_segment_display_1 (
    .g(segg_1_seg_g), .f(segf_1_seg_f), .a(sega_1_seg_a), .b(segb_1_seg_b), .e(sege_1_seg_e),
    .d(segd_1_seg_d), .c(segc_1_seg_c));  // open: dp
endmodule

module SegA (
  input  x0,
  input  x1,
  input  x2,
  input  x3,
  output SEG_A
);

  wire and_1_out, and_2_out, and_3_out, and_4_out, and_5_out, and_6_out, not_1_out, not_2_out, not_3_out,
       not_4_out;

  not not_1 (not_1_out, x0);
  not not_2 (not_2_out, x1);
  not not_3 (not_3_out, x2);
  not not_4 (not_4_out, x3);
  and and_1 (and_1_out, x0, not_2_out, not_3_out);
  and and_2 (and_2_out, not_1_out, x1, x3);
  and and_3 (and_3_out, x0, not_4_out);
  and and_4 (and_4_out, not_1_out, x2);
  and and_5 (and_5_out, x1, x2);
  and and_6 (and_6_out, not_2_out, not_4_out);
  or or_1 (SEG_A, and_1_out, and_2_out, and_3_out, and_4_out, and_5_out, and_6_out);
endmodule

module SegB (
  input  x0,
  input  x1,
  input  x2,
  input  x3,
  output SEG_B
);

  wire and_1_out, and_2_out, and_3_out, and_4_out, and_5_out, not_1_out, not_2_out, not_3_out, not_4_out;

  not not_1 (not_1_out, x0);
  not not_2 (not_2_out, x1);
  not not_3 (not_3_out, x2);
  not not_4 (not_4_out, x3);
  and and_1 (and_1_out, not_1_out, not_3_out, not_4_out);
  and and_2 (and_2_out, not_1_out, x2, x3);
  and and_3 (and_3_out, x0, not_3_out, x3);
  and and_4 (and_4_out, not_2_out, not_3_out);
  and and_5 (and_5_out, not_2_out, not_4_out);
  or or_1 (SEG_B, and_1_out, and_2_out, and_3_out, and_4_out, and_5_out);
endmodule

module SegC (
  input  x0,
  input  x1,
  input  x2,
  input  x3,
  output SEG_C
);

  wire and_1_out, and_2_out, and_3_out, and_4_out, and_5_out, not_1_out, not_2_out, not_3_out;

  not not_1 (not_1_out, x0);
  not not_2 (not_2_out, x1);
  not not_3 (not_3_out, x2);
  and and_1 (and_1_out, not_1_out, not_3_out);
  and and_2 (and_2_out, not_1_out, x3);
  and and_3 (and_3_out, not_3_out, x3);
  and and_4 (and_4_out, not_1_out, x1);
  and and_5 (and_5_out, x0, not_2_out);
  or or_1 (SEG_C, and_1_out, and_2_out, and_3_out, and_4_out, and_5_out);
endmodule

module SegD (
  input  x0,
  input  x1,
  input  x2,
  input  x3,
  output SEG_D
);

  wire and_1_out, and_2_out, and_3_out, and_4_out, and_5_out, not_1_out, not_2_out, not_3_out, not_4_out;

  not not_1 (not_1_out, x0);
  not not_2 (not_2_out, x1);
  not not_3 (not_3_out, x2);
  not not_4 (not_4_out, x3);
  and and_1 (and_1_out, not_1_out, not_2_out, not_4_out);
  and and_2 (and_2_out, not_2_out, x2, x3);
  and and_3 (and_3_out, x1, not_3_out, x3);
  and and_4 (and_4_out, x1, x2, not_4_out);
  and and_5 (and_5_out, x0, not_3_out);
  or or_1 (SEG_D, and_1_out, and_2_out, and_3_out, and_4_out, and_5_out);
endmodule

module SegE (
  input  x0,
  input  x1,
  input  x2,
  input  x3,
  output SEG_E
);

  wire and_1_out, and_2_out, and_3_out, and_4_out, not_1_out, not_2_out;

  not not_1 (not_1_out, x1);
  not not_2 (not_2_out, x3);
  and and_1 (and_1_out, not_1_out, not_2_out);
  and and_2 (and_2_out, x2, not_2_out);
  and and_3 (and_3_out, x0, x2);
  and and_4 (and_4_out, x0, x1);
  or or_1 (SEG_E, and_1_out, and_2_out, and_3_out, and_4_out);
endmodule

module SegF (
  input  x0,
  input  x1,
  input  x2,
  input  x3,
  output SEG_F
);

  wire and_1_out, and_2_out, and_3_out, and_4_out, and_5_out, not_1_out, not_2_out, not_3_out, not_4_out;

  not not_1 (not_1_out, x0);
  not not_2 (not_2_out, x1);
  not not_3 (not_3_out, x2);
  not not_4 (not_4_out, x3);
  and and_1 (and_1_out, not_1_out, x1, not_3_out);
  and and_2 (and_2_out, not_3_out, not_4_out);
  and and_3 (and_3_out, x1, not_4_out);
  and and_4 (and_4_out, x0, not_2_out);
  and and_5 (and_5_out, x0, x2);
  or or_1 (SEG_F, and_1_out, and_2_out, and_3_out, and_4_out, and_5_out);
endmodule

module SegG (
  input  x0,
  input  x1,
  input  x2,
  input  x3,
  output SEG_G
);

  wire and_1_out, and_2_out, and_3_out, and_4_out, and_5_out, not_1_out, not_2_out, not_3_out, not_4_out;

  not not_1 (not_1_out, x0);
  not not_2 (not_2_out, x1);
  not not_3 (not_3_out, x2);
  not not_4 (not_4_out, x3);
  and and_1 (and_1_out, not_1_out, x1, not_3_out);
  and and_2 (and_2_out, not_2_out, x2);
  and and_3 (and_3_out, x2, not_4_out);
  and and_4 (and_4_out, x0, not_2_out);
  and and_5 (and_5_out, x0, x3);
  or or_1 (SEG_G, and_1_out, and_2_out, and_3_out, and_4_out, and_5_out);
endmodule
